// Logisim project FlipFlops.circ as structural Verilog
module RS_KO (
  input  S,
  input  R,
  output Q
);

  wire nand_1_out, nand_2_out, nand_4_out;

  nand nand_1 (nand_1_out, S, S);
  nand nand_2 (nand_2_out, R, R);
  nand nand_3 (Q, nand_1_out, nand_4_out);
  nand nand_4 (nand_4_out, Q, nand_2_out);
endmodule

module RST_KO (
  input  S,
  input  T,
  input  R,
  output Q,
  output nQ
);

  wire nand_1_out, nand_2_out;

  nand nand_1 (nand_1_out, S, T);
  nand nand_2 (nand_2_out, T, R);
  nand nand_3 (Q, nand_1_out, nQ);
  nand nand_4 (nQ, Q, nand_2_out);
endmodule

module D_KO (
  input  D,
  input  CLK,
  output Q,
  output nQ
);

  wire not_1_out, not_2_out, not_3_out, rst_ko_1_nq, rst_ko_1_q;

  not not_1 (not_1_out, D);
  not not_2 (not_2_out, CLK);
  RST_KO rst_ko_1 (.S(D), .T(not_2_out), .R(not_1_out), .Q(rst_ko_1_q), .nQ(rst_ko_1_nq));
  not not_3 (not_3_out, not_2_out);
  RST_KO rst_ko_2 (.S(rst_ko_1_q), .T(not_3_out), .R(rst_ko_1_nq), .Q(Q), .nQ(nQ));
endmodule
